# Fritzing sketch Genius_game (saved by Fritzing 0.9.2b)
breadboards: 1

parts:
  Componente1 = Arduino Uno (Rev3)
  LED1 = LED - 5mm [color="Red (633nm)" package="5 mm [THT]"]
  R1 = Resistor [tolerance=±5% resistance=330 package=THT]
  LED2 = LED - 5mm [color="Blue (525nm)" package="5 mm [THT]"]
  R2 = Resistor [tolerance=±5% resistance=220 package=THT]
  S1 = Pushbutton [package="[THT]"]
  S2 = Pushbutton [package="[THT]"]
  LED3 = LED - 5mm [color="Yellow (595nm)" package="5 mm [THT]"]
  R3 = Resistor [tolerance=±5% resistance=220 package=THT]
  S3 = Pushbutton [package="[THT]"]
  LED4 = LED - 5mm [color="Green (570nm)" package="5 mm [THT]"]
  R4 = Resistor [tolerance=±5% resistance=220 package=THT]
  S4 = Pushbutton [package="[THT]"]

nets:
  N1: Componente1.D10_PWM/SS, S2.Pin_3, S2.Pin_4
  N2: Componente1.D11_PWM/MOSI, S1.Pin_3, S1.Pin_4
  N3: Componente1.D12/MISO, S3.Pin_3, S3.Pin_4
  N4: Componente1.D13/SCK, S4.Pin_3, S4.Pin_4
  N5: Componente1.GND, R1.Pin_1, R2.Pin_1, S1.Pin_1, S1.Pin_2, S2.Pin_1, S2.Pin_2, R3.Pin_1, S3.Pin_1, S3.Pin_2, R4.Pin_1, S4.Pin_1, S4.Pin_2
  N6: Componente1.D2, LED1.anode
  N7: Componente1.D3_PWM, LED2.anode
  N8: Componente1.D4, LED3.anode
  N9: Componente1.D5_PWM, LED4.anode
  N10: LED1.cathode, R1.Pin_0
  N11: LED2.cathode, R2.Pin_0
  N12: LED3.cathode, R3.Pin_0
  N13: LED4.cathode, R4.Pin_0
